// Logisim project CPU_4BITS.circ as structural Verilog: 10 circuits, main circuit main
module main (
  input  [3:0] B,
  input  [3:0] A,
  input  [1:0] x_y,
  output Overflow,
  output Overflow_2,
  output [3:0] S,
  output [3:0] S_2,
  output [3:0] S_3,
  output [3:0] S_4
);

  // Probe on B
  // Probe on A
  // Probe on S_3
  ADD_4 add_4_1 (.A(A), .Overflow(Overflow), .B(B), .out_4(S_3));
  SUB_4 sub_4_1 (.Overflow(Overflow_2), .A(A), .B(B), .out_4(S_4));
  // Probe on S_4
  Hot_Esq hot_esq_1 (.X_Y(x_y), .in_1(A), .out_3(S));
  Hot_Dir hot_dir_1 (.X_Y(x_y), .in_1(A), .out_3(S_2));
endmodule

module ADD_1 (
  input  C,
  input  A,
  input  B,
  output S,
  output Vai_1
);

  wire and_1_out, and_2_out, or_1_out, xor_1_out;

  or or_1 (or_1_out, C, B);
  xor xor_1 (xor_1_out, C, B);
  and and_1 (and_1_out, or_1_out, A);
  and and_2 (and_2_out, C, B);
  xor xor_2 (S, xor_1_out, A);
  or or_2 (Vai_1, and_1_out, and_2_out);
endmodule

module ADD_4 (
  input  [3:0] B,
  input  [3:0] A,
  output Overflow,
  output [3:0] out_4
);

  wire add_1_2_vai_1, add_1_3_vai_1, add_1_4_vai_1;

  ADD_1 add_1_1 (.C(add_1_2_vai_1), .S(out_4[3]), .Vai_1(Overflow), .A(A[3]), .B(B[3]));
  ADD_1 add_1_2 (.C(add_1_3_vai_1), .S(out_4[2]), .Vai_1(add_1_2_vai_1), .A(A[2]), .B(B[2]));
  ADD_1 add_1_3 (.C(add_1_4_vai_1), .S(out_4[1]), .Vai_1(add_1_3_vai_1), .A(A[1]), .B(B[1]));
  ADD_1 add_1_4 (.C(1'b0), .S(out_4[0]), .Vai_1(add_1_4_vai_1), .A(A[0]), .B(B[0]));
endmodule

module SUB_1 (
  input  A,
  input  B,
  input  VEM_1,
  output S,
  output VAI_1
);

  wire and_1_out, and_2_out, or_1_out, xor_1_out;

  xor xor_1 (xor_1_out, A, B);
  or or_1 (or_1_out, B, VEM_1);
  xor xor_2 (S, xor_1_out, VEM_1);
  and and_1 (and_1_out, or_1_out, ~A);  // AND_Gate
  and and_2 (and_2_out, VEM_1, B);
  or or_2 (VAI_1, and_1_out, and_2_out);
endmodule

module SUB_4 (
  input  [3:0] B,
  input  [3:0] A,
  output Overflow,
  output [3:0] out_4
);

  wire sub_1_2_vai_1, sub_1_3_vai_1, sub_1_4_vai_1;

  // Probe on A
  SUB_1 sub_1_1 (.S(out_4[3]), .A(A[3]), .B(B[3]), .VEM_1(sub_1_2_vai_1), .VAI_1(Overflow));
  SUB_1 sub_1_2 (.S(out_4[2]), .A(A[2]), .B(B[2]), .VEM_1(sub_1_3_vai_1), .VAI_1(sub_1_2_vai_1));
  // Probe on B
  SUB_1 sub_1_3 (.S(out_4[1]), .A(A[1]), .B(B[1]), .VEM_1(sub_1_4_vai_1), .VAI_1(sub_1_3_vai_1));
  // Probe on out_4
  SUB_1 sub_1_4 (.S(out_4[0]), .A(A[0]), .B(B[0]), .VEM_1(1'b0), .VAI_1(sub_1_4_vai_1));
endmodule

// Esq
module Hot_Esq (
  input  [3:0] in_1,
  input  [1:0] X_Y,
  output [3:0] out_3
);

  wire and_1_out, and_2_out, and_3_out, and_4_out, and_5_out, and_6_out, and_7_out, and_8_out, and_9_out;

  and and_1 (and_1_out, ~X_Y[1], ~X_Y[0], in_1[3]);  // AND_Gate
  and and_2 (and_2_out, ~X_Y[1], X_Y[0], in_1[2]);  // AND_Gate
  and and_3 (and_3_out, X_Y[1], ~X_Y[0], in_1[1]);  // AND_Gate
  and and_4 (and_4_out, X_Y[1], X_Y[0], in_1[0]);
  and and_5 (and_5_out, ~X_Y[1], ~X_Y[0], in_1[2]);  // AND_Gate
  and and_6 (and_6_out, ~X_Y[1], X_Y[0], in_1[1]);  // AND_Gate
  and and_7 (and_7_out, X_Y[1], ~X_Y[0], in_1[0]);  // AND_Gate
  and and_8 (and_8_out, ~X_Y[1], ~X_Y[0], in_1[1]);  // AND_Gate
  and and_9 (and_9_out, ~X_Y[1], X_Y[0], in_1[0]);  // AND_Gate
  and and_10 (out_3[0], ~X_Y[1], ~X_Y[0], in_1[0]);  // AND_Gate
  or or_1 (out_3[3], and_1_out, and_2_out, and_3_out, and_4_out);
  or or_2 (out_3[2], and_5_out, and_6_out, and_7_out);
  or or_3 (out_3[1], and_8_out, and_9_out);
endmodule

// Dir
module Hot_Dir (
  input  [3:0] in_1,
  input  [1:0] X_Y,
  output [3:0] out_3
);

  wire and_1_out, and_2_out, and_3_out, and_4_out, and_5_out, and_6_out, and_7_out, and_8_out, and_9_out;

  and and_1 (and_1_out, ~X_Y[1], ~X_Y[0], in_1[0]);  // AND_Gate
  and and_2 (and_2_out, ~X_Y[1], X_Y[0], in_1[1]);  // AND_Gate
  and and_3 (and_3_out, X_Y[1], ~X_Y[0], in_1[2]);  // AND_Gate
  and and_4 (and_4_out, X_Y[1], X_Y[0], in_1[3]);
  and and_5 (and_5_out, ~X_Y[1], ~X_Y[0], in_1[1]);  // AND_Gate
  and and_6 (and_6_out, ~X_Y[1], X_Y[0], in_1[2]);  // AND_Gate
  and and_7 (and_7_out, X_Y[1], ~X_Y[0], in_1[3]);  // AND_Gate
  and and_8 (and_8_out, ~X_Y[1], ~X_Y[0], in_1[2]);  // AND_Gate
  and and_9 (and_9_out, ~X_Y[1], X_Y[0], in_1[3]);  // AND_Gate
  and and_10 (out_3[3], ~X_Y[1], ~X_Y[0], in_1[3]);  // AND_Gate
  or or_1 (out_3[0], and_1_out, and_2_out, and_3_out, and_4_out);
  or or_2 (out_3[1], and_5_out, and_6_out, and_7_out);
  or or_3 (out_3[2], and_8_out, and_9_out);
endmodule

module Deco (
  input  [2:0] in_1,
  output S0,
  output S1,
  output S2,
  output S3,
  output S4,
  output S5,
  output S6,
  output S7
);

  wire not_1_out, not_2_out, not_3_out, not_4_out, not_5_out, not_6_out, not_7_out, not_8_out, not_9_out,
       not_10_out, not_11_out, not_12_out;

  not not_1 (not_1_out, in_1[2]);
  not not_2 (not_2_out, in_1[1]);
  not not_3 (not_3_out, in_1[0]);
  not not_4 (not_4_out, in_1[2]);
  not not_5 (not_5_out, in_1[1]);
  not not_6 (not_6_out, in_1[2]);
  not not_7 (not_7_out, in_1[0]);
  not not_8 (not_8_out, in_1[2]);
  not not_9 (not_9_out, in_1[1]);
  not not_10 (not_10_out, in_1[0]);
  not not_11 (not_11_out, in_1[1]);
  not not_12 (not_12_out, in_1[0]);
  and and_1 (S7, in_1[2], in_1[1], in_1[0]);
  and and_2 (S0, not_1_out, not_2_out, not_3_out);
  and and_3 (S1, not_4_out, not_5_out, in_1[0]);
  and and_4 (S2, not_6_out, in_1[1], not_7_out);
  and and_5 (S3, not_8_out, in_1[1], in_1[0]);
  and and_6 (S4, in_1[2], not_9_out, not_10_out);
  and and_7 (S5, in_1[2], not_11_out, in_1[0]);
  and and_8 (S6, in_1[2], in_1[1], not_12_out);
endmodule

module Buffer (
  input  [3:0] in_1,
  input  in_2,
  output [3:0] out_3
);

  assign out_3[3] = in_2 ? in_1[3] : 1'bz;  // Controlled_Buffer controlled_buffer_1
  assign out_3[2] = in_2 ? in_1[2] : 1'bz;  // Controlled_Buffer controlled_buffer_2
  assign out_3[1] = in_2 ? in_1[1] : 1'bz;  // Controlled_Buffer controlled_buffer_3
  assign out_3[0] = in_2 ? in_1[0] : 1'bz;  // Controlled_Buffer controlled_buffer_4
endmodule

module Or (
  output [3:0] out_1
);

  // OR_Gate or_1 is placed but not wired
endmodule
