// Logisim project add_1.circ as structural Verilog: 3 circuits, main circuit main
module main (
  input  A,
  input  B,
  input  VEM_1,
  output VAI_1,
  output S
);

  ADD_1 add_1_1 (.C(VEM_1), .S(S), .Vai_1(VAI_1), .A(A), .B(B));
endmodule

module ADD_1 (
  input  C,
  input  A,
  input  B,
  output S,
  output Vai_1
);

  wire and_1_out, and_2_out, or_1_out, xor_1_out;

  or or_1 (or_1_out, C, B);
  xor xor_1 (xor_1_out, C, B);
  and and_1 (and_1_out, or_1_out, A);
  and and_2 (and_2_out, C, B);
  xor xor_2 (S, xor_1_out, A);
  or or_2 (Vai_1, and_1_out, and_2_out);
endmodule

module ADD_4 (
  input  [3:0] B,
  input  [3:0] A,
  input  [3:0] S,
  output Overflow
);

  wire add_1_2_vai_1, add_1_3_vai_1, add_1_4_vai_1;

  ADD_1 add_1_1 (.C(add_1_2_vai_1), .S(S[3]), .Vai_1(Overflow), .A(A[3]), .B(B[3]));
  ADD_1 add_1_2 (.C(add_1_3_vai_1), .S(S[2]), .Vai_1(add_1_2_vai_1), .A(A[2]), .B(B[2]));
  ADD_1 add_1_3 (.C(add_1_4_vai_1), .S(S[1]), .Vai_1(add_1_3_vai_1), .A(A[1]), .B(B[1]));
  ADD_1 add_1_4 (.C(1'b0), .S(S[0]), .Vai_1(add_1_4_vai_1), .A(A[0]), .B(B[0]));
endmodule
