// Logisim project add_1.circ as structural Verilog: 5 circuits, main circuit main
module main (
  input  [3:0] B,
  input  [3:0] A,
  output Overflow,
  output Overflow_2,
  output [3:0] S,
  output [3:0] S_2
);

  ADD_4 add_4_1 (.A(A), .Overflow(Overflow), .S(S), .B(B));
  SUB_4 sub_4_1 (.Overflow(Overflow_2), .in_2(A), .in_3(S_2), .in_1(B));
endmodule

module ADD_1 (
  input  C,
  input  A,
  input  B,
  output S,
  output Vai_1
);

  wire and_1_out, and_2_out, or_1_out, xor_1_out;

  or or_1 (or_1_out, C, B);
  xor xor_1 (xor_1_out, C, B);
  and and_1 (and_1_out, or_1_out, A);
  and and_2 (and_2_out, C, B);
  xor xor_2 (S, xor_1_out, A);
  or or_2 (Vai_1, and_1_out, and_2_out);
endmodule

module ADD_4 (
  input  [3:0] B,
  input  [3:0] A,
  input  [3:0] S,
  output Overflow
);

  wire add_1_2_vai_1, add_1_3_vai_1, add_1_4_vai_1;

  ADD_1 add_1_1 (.C(add_1_2_vai_1), .S(S[3]), .Vai_1(Overflow), .A(A[3]), .B(B[3]));
  ADD_1 add_1_2 (.C(add_1_3_vai_1), .S(S[2]), .Vai_1(add_1_2_vai_1), .A(A[2]), .B(B[2]));
  ADD_1 add_1_3 (.C(add_1_4_vai_1), .S(S[1]), .Vai_1(add_1_3_vai_1), .A(A[1]), .B(B[1]));
  ADD_1 add_1_4 (.C(1'b0), .S(S[0]), .Vai_1(add_1_4_vai_1), .A(A[0]), .B(B[0]));
endmodule

module SUB_1 (
  input  A,
  input  B,
  input  VEM_1,
  output S,
  output VAI_1
);

  wire and_1_out, and_2_out, or_1_out, xor_1_out;

  xor xor_1 (xor_1_out, A, B);
  or or_1 (or_1_out, B, VEM_1);
  xor xor_2 (S, xor_1_out, VEM_1);
  and and_1 (and_1_out, or_1_out, ~A);  // AND_Gate
  and and_2 (and_2_out, VEM_1, B);
  or or_2 (VAI_1, and_1_out, and_2_out);
endmodule

module SUB_4 (
  input  [3:0] in_1,
  input  [3:0] in_2,
  input  [3:0] in_3,
  output Overflow
);

  wire sub_1_2_vai_1, sub_1_3_vai_1, sub_1_4_vai_1;

  // Probe on in_2
  SUB_1 sub_1_1 (.S(in_3[3]), .A(in_2[3]), .B(in_1[3]), .VEM_1(sub_1_2_vai_1), .VAI_1(Overflow));
  SUB_1 sub_1_2 (.S(in_3[2]), .A(in_2[2]), .B(in_1[2]), .VEM_1(sub_1_3_vai_1), .VAI_1(sub_1_2_vai_1));
  SUB_1 sub_1_3 (.S(in_3[1]), .A(in_2[1]), .B(in_1[1]), .VEM_1(sub_1_4_vai_1), .VAI_1(sub_1_3_vai_1));
  // Probe on in_3
  // Probe on in_1
  SUB_1 sub_1_4 (.S(in_3[0]), .A(in_2[0]), .B(in_1[0]), .VEM_1(1'b0), .VAI_1(sub_1_4_vai_1));
endmodule
