// Logisim project trab.circ as structural Verilog: 16 circuits, main circuit main
module main (
);

  wire button_1_out, clock_1_out, not_1_out, not_2_out, OVERFLOW_q, uc_1_d, uc_1_e, uc_1_load, uc_1_out_11,
       uc_1_out_12, uc_1_out_13, uc_1_out_14, uc_1_out_15, uc_1_r_w, ula_1_overflow, ula_1_zero, ZERO_q;
  wire [2:0] uc_1_opcode;
  wire [3:0] ac_1_out_3, counter_1_q, mux_1_out_4, ram_1_data, \uc_1_endereço , uc_1_operando, ula_1_s;
  wire [7:0] ir_1_s, rom_1_data;

  Counter #(.width(4), .max('hf)) counter_1 (
    .load(uc_1_load), .D(uc_1_operando), .count(not_1_out), .Q(counter_1_q), .clk(uc_1_out_12),
    .clr(uc_1_out_15));  // open: carry
  not not_1 (not_1_out, uc_1_load);
  Clock clock_1 (.out(clock_1_out));
  Button button_1 (.out(button_1_out));
  IR ir_1 (.CLOCK(uc_1_out_11), .E(rom_1_data), .S(ir_1_s));
  ROM #(.addrWidth(4)) rom_1 (.addr(counter_1_q), .data(rom_1_data));  // open: sel
  UC uc_1 (
    .\INSTRUÇÃO (ir_1_s), .OPERANDO(uc_1_operando), .E(uc_1_e), .OPCODE(uc_1_opcode),
    .\ENDEREÇO (\uc_1_endereço ), .LOAD(uc_1_load), .in_3(clock_1_out), .in_5(button_1_out),
    .out_15(uc_1_out_15), .out_11(uc_1_out_11), .out_12(uc_1_out_12), .out_13(uc_1_out_13),
    .out_14(uc_1_out_14), .Z(ZERO_q), .O(OVERFLOW_q), .R_W(uc_1_r_w), .D(uc_1_d));
  MUX mux_1 (.C(uc_1_d), .E(\uc_1_endereço ), .D(ram_1_data), .out_4(mux_1_out_4));
  // Probe on ac_1_out_3
  // Probe on mux_1_out_4
  ULA ula_1 (
    .in_1(uc_1_r_w), .B(mux_1_out_4), .A(ac_1_out_3), .in_4(uc_1_opcode), .Zero(ula_1_zero),
    .Overflow(ula_1_overflow), .S(ula_1_s));
  AC ac_1 (.in_1(uc_1_out_13), .in_2(ula_1_s), .out_3(ac_1_out_3));
  // Probe on ac_1_out_3
  D_Flip_Flop OVERFLOW (.clk(uc_1_out_13), .D(ula_1_overflow), .Q(OVERFLOW_q));  // open: Qn, preset, en, reset
  D_Flip_Flop ZERO (.clk(uc_1_out_13), .D(ula_1_zero), .Q(ZERO_q));  // open: Qn, preset, en, reset
  RAM #(.addrWidth(4), .dataWidth(4)) ram_1 (
    .addr(\uc_1_endereço ), .data(ram_1_data), .sel(uc_1_out_14), .ld(uc_1_e));  // open: clk, clr
  not not_2 (not_2_out, uc_1_e);
  Buffer buffer_1 (.in_1(ac_1_out_3), .in_2(not_2_out), .out_3(ram_1_data));
endmodule

module ADD_1 (
  input  C,
  input  A,
  input  B,
  output S,
  output Vai_1
);

  wire and_1_out, and_2_out, or_1_out, xor_1_out;

  or or_1 (or_1_out, C, B);
  xor xor_1 (xor_1_out, C, B);
  and and_1 (and_1_out, or_1_out, A);
  and and_2 (and_2_out, C, B);
  xor xor_2 (S, xor_1_out, A);
  or or_2 (Vai_1, and_1_out, and_2_out);
endmodule

module ADD_4 (
  input  [3:0] B,
  input  [3:0] A,
  output Overflow,
  output [3:0] out_4
);

  wire add_1_2_vai_1, add_1_3_vai_1, add_1_4_vai_1;

  ADD_1 add_1_1 (.C(add_1_2_vai_1), .S(out_4[3]), .Vai_1(Overflow), .A(A[3]), .B(B[3]));
  ADD_1 add_1_2 (.C(add_1_3_vai_1), .S(out_4[2]), .Vai_1(add_1_2_vai_1), .A(A[2]), .B(B[2]));
  ADD_1 add_1_3 (.C(add_1_4_vai_1), .S(out_4[1]), .Vai_1(add_1_3_vai_1), .A(A[1]), .B(B[1]));
  ADD_1 add_1_4 (.C(1'b0), .S(out_4[0]), .Vai_1(add_1_4_vai_1), .A(A[0]), .B(B[0]));
endmodule

module SUB_1 (
  input  A,
  input  B,
  input  VEM_1,
  output S,
  output VAI_1
);

  wire and_1_out, and_2_out, or_1_out, xor_1_out;

  xor xor_1 (xor_1_out, A, B);
  or or_1 (or_1_out, B, VEM_1);
  xor xor_2 (S, xor_1_out, VEM_1);
  and and_1 (and_1_out, or_1_out, ~A);  // AND_Gate
  and and_2 (and_2_out, VEM_1, B);
  or or_2 (VAI_1, and_1_out, and_2_out);
endmodule

module SUB_4 (
  input  [3:0] B,
  input  [3:0] A,
  output Overflow,
  output [3:0] out_4
);

  wire sub_1_2_vai_1, sub_1_3_vai_1, sub_1_4_vai_1;

  // Probe on A
  SUB_1 sub_1_1 (.S(out_4[3]), .A(A[3]), .B(B[3]), .VEM_1(sub_1_2_vai_1), .VAI_1(Overflow));
  SUB_1 sub_1_2 (.S(out_4[2]), .A(A[2]), .B(B[2]), .VEM_1(sub_1_3_vai_1), .VAI_1(sub_1_2_vai_1));
  // Probe on B
  SUB_1 sub_1_3 (.S(out_4[1]), .A(A[1]), .B(B[1]), .VEM_1(sub_1_4_vai_1), .VAI_1(sub_1_3_vai_1));
  // Probe on out_4
  SUB_1 sub_1_4 (.S(out_4[0]), .A(A[0]), .B(B[0]), .VEM_1(1'b0), .VAI_1(sub_1_4_vai_1));
endmodule

// Esq
module Hot_Esq (
  input  [3:0] in_1,
  input  [1:0] X_Y,
  output [3:0] out_3
);

  wire and_1_out, and_2_out, and_3_out, and_4_out, and_5_out, and_6_out, and_7_out, and_8_out, and_9_out;

  and and_1 (and_1_out, ~X_Y[1], ~X_Y[0], in_1[3]);  // AND_Gate
  and and_2 (and_2_out, ~X_Y[1], X_Y[0], in_1[2]);  // AND_Gate
  and and_3 (and_3_out, X_Y[1], ~X_Y[0], in_1[1]);  // AND_Gate
  and and_4 (and_4_out, X_Y[1], X_Y[0], in_1[0]);
  and and_5 (and_5_out, ~X_Y[1], ~X_Y[0], in_1[2]);  // AND_Gate
  and and_6 (and_6_out, ~X_Y[1], X_Y[0], in_1[1]);  // AND_Gate
  and and_7 (and_7_out, X_Y[1], ~X_Y[0], in_1[0]);  // AND_Gate
  and and_8 (and_8_out, ~X_Y[1], ~X_Y[0], in_1[1]);  // AND_Gate
  and and_9 (and_9_out, ~X_Y[1], X_Y[0], in_1[0]);  // AND_Gate
  and and_10 (out_3[0], ~X_Y[1], ~X_Y[0], in_1[0]);  // AND_Gate
  or or_1 (out_3[3], and_1_out, and_2_out, and_3_out, and_4_out);
  or or_2 (out_3[2], and_5_out, and_6_out, and_7_out);
  or or_3 (out_3[1], and_8_out, and_9_out);
endmodule

// Dir
module Hot_Dir (
  input  [3:0] in_1,
  input  [1:0] X_Y,
  output [3:0] out_3
);

  wire and_1_out, and_2_out, and_3_out, and_4_out, and_5_out, and_6_out, and_7_out, and_8_out, and_9_out;

  and and_1 (and_1_out, ~X_Y[1], ~X_Y[0], in_1[0]);  // AND_Gate
  and and_2 (and_2_out, ~X_Y[1], X_Y[0], in_1[1]);  // AND_Gate
  and and_3 (and_3_out, X_Y[1], ~X_Y[0], in_1[2]);  // AND_Gate
  and and_4 (and_4_out, X_Y[1], X_Y[0], in_1[3]);
  and and_5 (and_5_out, ~X_Y[1], ~X_Y[0], in_1[1]);  // AND_Gate
  and and_6 (and_6_out, ~X_Y[1], X_Y[0], in_1[2]);  // AND_Gate
  and and_7 (and_7_out, X_Y[1], ~X_Y[0], in_1[3]);  // AND_Gate
  and and_8 (and_8_out, ~X_Y[1], ~X_Y[0], in_1[2]);  // AND_Gate
  and and_9 (and_9_out, ~X_Y[1], X_Y[0], in_1[3]);  // AND_Gate
  and and_10 (out_3[3], ~X_Y[1], ~X_Y[0], in_1[3]);  // AND_Gate
  or or_1 (out_3[0], and_1_out, and_2_out, and_3_out, and_4_out);
  or or_2 (out_3[1], and_5_out, and_6_out, and_7_out);
  or or_3 (out_3[2], and_8_out, and_9_out);
endmodule

// DEC
module Deco (
  input  [2:0] in_1,
  output S0,
  output S1,
  output S2,
  output S3,
  output S4,
  output S5,
  output S6,
  output S7
);

  wire not_1_out, not_2_out, not_3_out, not_4_out, not_5_out, not_6_out, not_7_out, not_8_out, not_9_out,
       not_10_out, not_11_out, not_12_out;

  not not_1 (not_1_out, in_1[2]);
  not not_2 (not_2_out, in_1[1]);
  not not_3 (not_3_out, in_1[0]);
  not not_4 (not_4_out, in_1[2]);
  not not_5 (not_5_out, in_1[1]);
  not not_6 (not_6_out, in_1[2]);
  not not_7 (not_7_out, in_1[0]);
  not not_8 (not_8_out, in_1[2]);
  not not_9 (not_9_out, in_1[1]);
  not not_10 (not_10_out, in_1[0]);
  not not_11 (not_11_out, in_1[1]);
  not not_12 (not_12_out, in_1[0]);
  and and_1 (S7, in_1[2], in_1[1], in_1[0]);
  and and_2 (S0, not_1_out, not_2_out, not_3_out);
  and and_3 (S1, not_4_out, not_5_out, in_1[0]);
  and and_4 (S2, not_6_out, in_1[1], not_7_out);
  and and_5 (S3, not_8_out, in_1[1], in_1[0]);
  and and_6 (S4, in_1[2], not_9_out, not_10_out);
  and and_7 (S5, in_1[2], not_11_out, in_1[0]);
  and and_8 (S6, in_1[2], in_1[1], not_12_out);
endmodule

// BUFF
module Buffer (
  input  [3:0] in_1,
  input  in_2,
  output [3:0] out_3
);

  assign out_3[3] = in_2 ? in_1[3] : 1'bz;  // Controlled_Buffer controlled_buffer_1
  assign out_3[2] = in_2 ? in_1[2] : 1'bz;  // Controlled_Buffer controlled_buffer_2
  assign out_3[1] = in_2 ? in_1[1] : 1'bz;  // Controlled_Buffer controlled_buffer_3
  assign out_3[0] = in_2 ? in_1[0] : 1'bz;  // Controlled_Buffer controlled_buffer_4
endmodule

// OR_4
module Or (
  input  [3:0] B,
  input  [3:0] A,
  output [3:0] out_3
);

  or or_1 (out_3[3], A[3], B[3]);
  or or_2 (out_3[2], A[2], B[2]);
  or or_3 (out_3[1], A[1], B[1]);
  or or_4 (out_3[0], A[0], B[0]);
endmodule

// NOT
module Not (
  input  [3:0] E,
  output [3:0] S
);

  not not_1 (S[2], E[2]);
  not not_2 (S[3], E[3]);
  not not_3 (S[0], E[0]);
  not not_4 (S[1], E[1]);
endmodule

module ULA (
  input  in_1,
  input  [3:0] B,
  input  [3:0] A,
  input  [2:0] in_4,
  output Overflow,
  output [3:0] S,
  output Zero
);

  wire add_4_1_overflow, and_1_out, and_2_out, deco_1_s0, deco_1_s1, deco_1_s2, deco_1_s3, deco_1_s4,
       deco_1_s5, deco_1_s6, deco_1_s7, not_2_out, sub_4_1_overflow;
  wire [3:0] add_4_1_out_4, buffer_6_out_3, hot_dir_1_out_3, hot_esq_1_out_3, not_1_s, or_2_out_3,
       sub_4_1_out_4;

  and and_1 (and_1_out, add_4_1_overflow, deco_1_s1);
  or or_1 (Overflow, and_1_out, and_2_out);
  and and_2 (and_2_out, sub_4_1_overflow, deco_1_s2);
  Buffer buffer_1 (.in_1(B), .in_2(deco_1_s0), .out_3(S));
  Deco deco_1 (
    .in_1(in_4), .S0(deco_1_s0), .S1(deco_1_s1), .S2(deco_1_s2), .S3(deco_1_s3), .S4(deco_1_s4),
    .S5(deco_1_s5), .S6(deco_1_s6), .S7(deco_1_s7));
  SUB_4 sub_4_1 (.Overflow(sub_4_1_overflow), .A(A), .B(B), .out_4(sub_4_1_out_4));
  ADD_4 add_4_1 (.A(A), .Overflow(add_4_1_overflow), .B(B), .out_4(add_4_1_out_4));
  Buffer buffer_2 (.in_1(add_4_1_out_4), .in_2(deco_1_s1), .out_3(S));
  Or or_2 (.B(B), .A(A), .out_3(or_2_out_3));
  Buffer buffer_3 (.in_1(or_2_out_3), .in_2(deco_1_s3), .out_3(S));
  Buffer buffer_4 (.in_1(sub_4_1_out_4), .in_2(deco_1_s2), .out_3(S));
  nor nor_1 (Zero, S[0], S[1], S[2], S[3], deco_1_s6, deco_1_s7);
  Not not_1 (.E(B), .S(not_1_s));
  Buffer buffer_5 (.in_1(not_1_s), .in_2(deco_1_s4), .out_3(S));
  Hot_Esq hot_esq_1 (.X_Y(B[1:0]), .in_1(A), .out_3(hot_esq_1_out_3));
  Hot_Dir hot_dir_1 (.X_Y(B[1:0]), .in_1(A), .out_3(hot_dir_1_out_3));
  Buffer buffer_6 (.in_1(hot_esq_1_out_3), .in_2(not_2_out), .out_3(buffer_6_out_3));
  not not_2 (not_2_out, in_1);
  Buffer buffer_7 (.in_1(hot_dir_1_out_3), .in_2(in_1), .out_3(buffer_6_out_3));
  Buffer buffer_8 (.in_1(buffer_6_out_3), .in_2(deco_1_s5), .out_3(S));
endmodule

module AC (
  input  in_1,
  input  [3:0] in_2,
  output [3:0] out_3
);

  D_Flip_Flop d_ff_1 (.clk(in_1), .D(in_2[3]), .Q(out_3[3]));  // open: Qn, preset, en, reset
  D_Flip_Flop d_ff_2 (.clk(in_1), .D(in_2[2]), .Q(out_3[2]));  // open: Qn, preset, en, reset
  D_Flip_Flop d_ff_3 (.clk(in_1), .D(in_2[1]), .Q(out_3[1]));  // open: Qn, preset, en, reset
  D_Flip_Flop d_ff_4 (.clk(in_1), .D(in_2[0]), .Q(out_3[0]));  // open: Qn, preset, en, reset
endmodule

module MUX (
  input  [3:0] E,
  input  [3:0] D,
  input  C,
  output [3:0] out_4
);

  wire not_1_out;

  not not_1 (not_1_out, C);
  Buffer buffer_1 (.in_1(E), .in_2(not_1_out), .out_3(out_4));
  Buffer buffer_2 (.in_1(D), .in_2(C), .out_3(out_4));
endmodule

// UNIDADE DE CONTROLE
module UC (
  input  [7:0] \INSTRUÇÃO ,
  input  Z,
  input  in_3,
  input  O,
  input  in_5,
  output [3:0] \ENDEREÇO ,
  output [3:0] OPERANDO,
  output [2:0] OPCODE,
  output D,
  output E,
  output out_11,
  output out_12,
  output out_13,
  output out_14,
  output out_15,
  output LOAD,
  output R_W
);

  wire and_1_out, and_2_out, and_3_out, GOTO_out, nand_1_out;
  wire [1:0] counter_1_q;

  Counter #(.width(2), .max('h3)) counter_1 (.Q(counter_1_q), .clk(in_3), .clr(in_5));  // open: load, D, count, carry
  and IR (out_11, ~counter_1_q[1], ~counter_1_q[0]);  // AND_Gate
  and PC (out_12, ~counter_1_q[1], counter_1_q[0]);  // AND_Gate
  and RAM (out_14, counter_1_q[1], counter_1_q[0]);
  and AC (out_13, counter_1_q[1], ~counter_1_q[0]);  // AND_Gate
  and and_1 (and_1_out, out_13, \INSTRUÇÃO [7], \INSTRUÇÃO [6], \INSTRUÇÃO [5], \INSTRUÇÃO [4]);
  not not_1 (R_W, and_1_out);
  and and_2 (and_2_out, \INSTRUÇÃO [7], \INSTRUÇÃO [6], ~\INSTRUÇÃO [5], \INSTRUÇÃO [4], out_12, O);  // AND_Gate
  and and_3 (and_3_out, \INSTRUÇÃO [7], \INSTRUÇÃO [6], ~\INSTRUÇÃO [5], ~\INSTRUÇÃO [4], Z, out_12);  // AND_Gate
  and GOTO (GOTO_out, out_12, \INSTRUÇÃO [7], \INSTRUÇÃO [6], \INSTRUÇÃO [5], ~\INSTRUÇÃO [4]);  // AND_Gate
  nand nand_1 (nand_1_out, \INSTRUÇÃO [7], ~\INSTRUÇÃO [6], \INSTRUÇÃO [5]);  // NAND_Gate
  or or_1 (LOAD, GOTO_out, and_3_out, and_2_out);
  and and_4 (E, \INSTRUÇÃO [4], nand_1_out);

  assign D = \INSTRUÇÃO [4];
  assign \ENDEREÇO  = \INSTRUÇÃO [3:0];
  assign OPCODE = \INSTRUÇÃO [7:5];
  assign OPERANDO = \INSTRUÇÃO [3:0];
  assign out_15 = in_5;
endmodule

module IR (
  input  CLOCK,
  input  [7:0] E,
  output [7:0] S
);

  D_Flip_Flop d_ff_1 (.clk(CLOCK), .D(E[7]), .Q(S[7]));  // open: Qn, preset, en, reset
  D_Flip_Flop d_ff_2 (.clk(CLOCK), .D(E[6]), .Q(S[6]));  // open: Qn, preset, en, reset
  D_Flip_Flop d_ff_3 (.clk(CLOCK), .D(E[5]), .Q(S[5]));  // open: Qn, preset, en, reset
  D_Flip_Flop d_ff_4 (.clk(CLOCK), .D(E[4]), .Q(S[4]));  // open: Qn, preset, en, reset
  D_Flip_Flop d_ff_5 (.clk(CLOCK), .D(E[3]), .Q(S[3]));  // open: Qn, preset, en, reset
  D_Flip_Flop d_ff_6 (.clk(CLOCK), .D(E[2]), .Q(S[2]));  // open: Qn, preset, en, reset
  D_Flip_Flop d_ff_7 (.clk(CLOCK), .D(E[1]), .Q(S[1]));  // open: Qn, preset, en, reset
  D_Flip_Flop d_ff_8 (.clk(CLOCK), .D(E[0]), .Q(S[0]));  // open: Qn, preset, en, reset
endmodule
